# Fritzing sketch schematicA (saved by Fritzing 0.9.5d)
breadboards: 1

parts:
  R1 = Resistor [tolerance=±5% resistance=220 package="0805 [SMD]"]
  R2 = Resistor [tolerance=±5% resistance=220 package="0805 [SMD]"]
  R3 = Resistor [tolerance=±5% resistance=220 package="0805 [SMD]"]
  R4 = Resistor [tolerance=±5% resistance=220 package="0805 [SMD]"]
  Part1 = Adafruit T-Cobbler Plus [part_number="Adafruit #1989 and #2028"]
  HC-SR04_Sensor_1 = HC-SR04 Ultrasonic Distance Sensor
  LED1 = LED - 3mm [color="Red (633nm)" package="3 mm [THT]"]
  S1 = Pushbutton [package="[SMD]"]

nets:
  N1: R1.Pin_0, R2.Pin_0
  N2: R1.Pin_1, HC-SR04_Sensor_1.ECHO
  N3: R2.Pin_1, R3.Pin_0
  GND: R3.Pin_1, Part1.GND, HC-SR04_Sensor_1.GND, LED1.anode, S1.Pin_1, S1.Pin_2
  N4: R4.Pin_0, Part1.GPIO25
  N5: R4.Pin_1, LED1.cathode
  N6: Part1.GPIO26, S1.Pin_3, S1.Pin_4
  +5V: Part1.+5V, HC-SR04_Sensor_1.VCC
  N7: Part1.GPIO23, HC-SR04_Sensor_1.TRIG

custom parts:
  Adafruit T-Cobbler Plus: The Raspberry Pi has landed on the Maker World like a 40-GPIO pinned, quad-USB ported, credit card sized bomb of DIY joy. And while you can use most of our great Model B accessories by hooking up our downgrade cable, its probably a good time to upgrade your set up and accessorize using all of the 40 pins. That's why we now carry the Assembled Adafruit Pi T-Cobbler Plus - Breakout + Cable for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
